# Fritzing sketch circuit (saved by Fritzing 0.9.4)
breadboards: 1

parts:
  Mod1 = gy-906
  LCM1602_IIC1 = LCM1602 IIC [part_number="LCM1602 IIC" chip_label="LCM1602 IIC" package="DIP (Dual Inline) [THT]"]
  부품1 = Arduino Uno (Rev3)

nets:
  VIN: Mod1.VIN, LCM1602_IIC1.VCC, 부품1.5V
  GND: Mod1.GND, LCM1602_IIC1.GND, 부품1.GND
  N1: Mod1.SCL, LCM1602_IIC1.SCL, 부품1.A5/SCL
  N2: Mod1.SDA, LCM1602_IIC1.SDA, 부품1.A4/SDA

notes:
  VCC/VIN : 빨간색
  GND : 검정색
  SCL : 보라색
  SDA : 노란색

custom parts:
  gy-906: gy-906 Non-contact PIR I2C interface temperature sensor breakout board.
  LCM1602 IIC: I2C-Module to use a 1602 or 2004 LCD on with the wire.h libory Serial LCD Modul
